# Fritzing sketch car1 (saved by Fritzing 0.9.2b)
breadboards: 1

parts:
  Part1 = Arduino Uno (Rev3)
  LCD1 = LCD screen
  IR1 = TSOP312.., 314.. [package=THT]
  IC1 = ULN2003A [package="DIP16 [THT]"]
  M1 = Stepper Motor - Unipolar
  M2 = Stepper Motor - Unipolar

nets:
  N1: Part1.D8, IC1.Out_7
  N2: Part1.D9_PWM, IC1.Out_6
  N3: Part1.D10_PWM/SS, IC1.Out_5
  N4: Part1.D11_PWM/MOSI, LCD1.E
  N5: Part1.D12/MISO, LCD1.RS
  N6: Part1.D13/SCK, IR1.Data
  GND: Part1.GND, LCD1.VSS, LCD1.R/W, LCD1.LED-, IR1.GND, IC1.Out_1
  N7: Part1.D2, LCD1.DB7
  N8: Part1.D3_PWM, LCD1.DB6
  N9: Part1.D4, LCD1.DB5
  N10: Part1.D5_PWM, LCD1.DB4
  N11: Part1.D6_PWM, LCD1.V0
  N12: Part1.D7, IC1.COM_-_Common
  5V: Part1.5V, LCD1.VDD, LCD1.LED+, IR1.Vs, IC1.In_1, M1.A, M1.B, M2.A, M2.B
  N13: IC1.In_5, M1.COMMON_1, M2.COMMON_1
  N14: IC1.In_6, M1.C, M2.C
  N15: IC1.In_7, M1.COMMON_2, M2.COMMON_2
  N16: IC1.0V, M1.D, M2.D
