# Fritzing sketch light (saved by Fritzing 0.9.2b)
breadboards: 1

parts:
  Part1 = Arduino Uno (Rev3)
  LED2 = LED - 5mm [color="Yellow (595nm)" package="5 mm [THT]"]
  LED3 = LED - 5mm [color="Green (555nm)" package="5 mm [THT]"]
  R1 = Resistor [tolerance=±5% resistance=220 package=THT]
  R2 = Resistor [tolerance=±5% resistance=220 package=THT]
  R3 = Resistor [tolerance=±5% resistance=220 package=THT]
  LCD1 = LCD screen
  IR1 = TSOP312.., 314.. [package=THT]
  LED1 = smd LED [color="Red (633nm)" package="0603 [SMD]"]
  LED1_2 = smd LED [color="Red (633nm)" package="0805 [SMD]"]

nets:
  N1: Part1.D8, R2.Pin_1
  N2: Part1.D11_PWM/MOSI, LCD1.E
  N3: Part1.D12/MISO, LCD1.RS
  N4: Part1.D13/SCK, IR1.GND
  GND: Part1.GND, LCD1.VSS, LCD1.R/W, LCD1.LED-, IR1.Vs
  N5: Part1.D2, LCD1.DB7
  N6: Part1.D3_PWM, LCD1.DB6
  N7: Part1.D4, LCD1.DB5
  N8: Part1.D5_PWM, LCD1.DB4
  N9: Part1.D6_PWM, LCD1.V0
  N10: Part1.D7, R3.Pin_1
  5V: Part1.5V, LED2.cathode, LED3.cathode, R2.Pin_0, LCD1.VDD, LCD1.LED+, IR1.Data, LED1.cathode, LED1_2.cathode
  N11: LED3.anode, R3.Pin_0
  N12: R1.Pin_0, LED1.anode, LED1_2.anode
