# Fritzing sketch Untitled Sketch (saved by Fritzing 0.9.2b)
breadboards: 2

parts:
  Part1 = Arduino Uno (Rev3)
  IC1 = ULN2003A [package="DIP16 [THT]"]

nets:
  N1: Part1.D8, IC1.In_1
  N2: Part1.D9_PWM, IC1.In_2
  N3: Part1.D10_PWM/SS, IC1.In_3
  N4: Part1.D11_PWM/MOSI, IC1.In_4
  N5: Part1.5V, IC1.0V, IC1.COM_-_Common
